# Fritzing sketch Sketch (saved by Fritzing 0.9.10b)
breadboards: 1

parts:
  HC-SR04_Sensor_1 = HC-SR04 Ultrasonic Distance Sensor
  Mod1 = Heltec WiFi LoRa 32 V2 [part_number=HTIT-WB32LA]

nets:
  N1: HC-SR04_Sensor_1.VCC, Mod1.pin_20
  N2: HC-SR04_Sensor_1.TRIG, Mod1.pin_35
  N3: HC-SR04_Sensor_1.ECHO, Mod1.pin_33
  GND: HC-SR04_Sensor_1.GND, Mod1.GND
  N4: Mod1.pin_16, Mod1.pin_17
  N5: Mod1.pin_21, Mod1.pin_22
